# Fritzing sketch ESP32-CAM_Car_circuit (saved by Fritzing 0.9.3b)

parts:
  ESP32_-_Back1 = ESP32 - CAM
  L298N1 = L298N DC motor driver
  Part1 = SRF05 Ultrasonic Rangefinder
  M1 = Getriebemotor
  M2 = Getriebemotor
  VCC1 = Battery  # not connected

nets:
  N1: ESP32_-_Back1.GPIO2, L298N1.5V#9, L298N1.5V#10, L298N1.ENA, L298N1.ENB
  N2: ESP32_-_Back1.GPIO14, L298N1.IN4
  N3: ESP32_-_Back1.GPIO15, L298N1.IN3
  N4: ESP32_-_Back1.GPIO13, L298N1.IN2
  N5: ESP32_-_Back1.GPIO12, L298N1.IN1
  GND: ESP32_-_Back1.GND, L298N1.GND
  N6: ESP32_-_Back1.5V, L298N1.5V#7
  N7: ESP32_-_Back1.GPIO3_/_RX, Part1.Trig
  N8: ESP32_-_Back1.GPIO1_/_TX, Part1.Echo
  N9: L298N1.OUT1, M2.pin_2
  N10: L298N1.OUT2, M2.pin_1
  N11: L298N1.OUT3, M1.pin_2
  N12: L298N1.OUT4, M1.pin_1

notes:
  Final design on 19th June, 2023 - Monday
  These should be 18650 LiPo cells - 4x

custom parts:
  ESP32 - CAM: The ESP32-CAM has a very competitive small-size camera module that can operate independently as a minimum system with a footprint of only 27*40.5*4.5mm and a deep sleep current of up to 6mA.
  L298N DC motor driver: 2x DC motor driver with 78M05 positive voltage regulator (7..35 V) L298N: max 46 V, 2 A Set 5 V Enable jumper to enable 5 V regultor (needed for the L298N) and +5 V output at screw terminal or supply external +5 V at screw terminal Set ENA and/or ENB to +5 V to enable motor permanently or supply ENA and/or ENB with PWM signal IN1 and IN2 set rotation directory for motor A (OUT1/OUT2) IN2 and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
